// Logisim project Milestone_1_(33405).circ as structural Verilog: 38 circuits, main circuit main
module main (
);

  ALU_toy8 alu_toy8_1 ();  // open: A, B, S2, S1, S0, result
  MUX_8bittoy8 mux_8bittoy8_1 ();  // open: I_0, I_1, I_2, I_3, S_0, S_1, answer
  De_coder de_coder_1 ();  // open: I2, I1, I0, in_4, O, i, ii, iii, iv, v, vi, vii
  fulladderfortoy8 fulladderfortoy8_1 ();  // open: A, B, Cin, sum, Cout
  one_hot_mux one_hot_mux_1 ();  // open: A, B, C, D, E, F, I1, I2, I3, I4, I5, I6, decision
  DMUX_toy8 dmux_toy8_1 ();  // open: I, S_0, S_1, O_0, O_1, O_2, O_3
endmodule

module xorimplement (
  input  A,
  input  B,
  output xorout
);

  wire andgate_1_out_3, andgate_2_out_3, andgate_3_out_3, notgate_1_out_2, notgate_2_out_2, orgate_1_orout;

  andgate andgate_1 (.A(A), .B(B), .out_3(andgate_1_out_3));
  andgate andgate_2 (.A(A), .B(B), .out_3(andgate_2_out_3));
  orgate orgate_1 (.A(A), .B(B), .orout(orgate_1_orout));
  notgate notgate_1 (.in_1(andgate_1_out_3), .out_2(notgate_1_out_2));
  notgate notgate_2 (.in_1(andgate_2_out_3), .out_2(notgate_2_out_2));
  andgate andgate_3 (.A(notgate_1_out_2), .B(notgate_2_out_2), .out_3(andgate_3_out_3));
  andgate andgate_4 (.A(andgate_3_out_3), .B(orgate_1_orout), .out_3(xorout));
endmodule

module andgate (
  input  A,
  input  B,
  output out_3
);

  wire nandgate_1_nandoutput;

  nandgate nandgate_1 (.A(A), .B(B), .nandoutput(nandgate_1_nandoutput));
  notgate notgate_1 (.in_1(nandgate_1_nandoutput), .out_2(out_3));
endmodule

module orgate (
  input  A,
  input  B,
  output orout
);

  wire norgate_1_norout;

  norgate norgate_1 (.A(A), .B(B), .norout(norgate_1_norout));
  notgate notgate_1 (.in_1(norgate_1_norout), .out_2(orout));
endmodule

module notgate (
  input  in_1,
  output out_2
);

  Pull_Resistor pull_resistor_1 (.node(out_2));
  Transistor transistor_1 (.in(1'b1), .out(out_2), .gate(in_1));
endmodule

module nandgate (
  input  A,
  input  B,
  output nandoutput
);

  wire transistor_3_out;

  Transistor transistor_1 (.in(1'b1), .out(nandoutput), .gate(A));
  Transistor #(.\type ("n")) transistor_2 (.in(transistor_3_out), .out(nandoutput), .gate(A));
  Transistor #(.\type ("n")) transistor_3 (.in(1'b0), .out(transistor_3_out), .gate(B));
  Transistor transistor_4 (.in(1'b1), .out(nandoutput), .gate(B));
endmodule

module norgate (
  input  A,
  input  B,
  output norout
);

  wire transistor_1_out;

  Transistor transistor_1 (.in(1'b1), .out(transistor_1_out), .gate(A));
  Transistor transistor_2 (.in(transistor_1_out), .out(norout), .gate(B));
  Transistor #(.\type ("n")) transistor_3 (.in(1'b0), .out(norout), .gate(A));
  Transistor #(.\type ("n")) transistor_4 (.in(1'b0), .out(norout), .gate(B));
endmodule

module classwork (
  input  R
);

  wire clock, comparator_1_eq, comparator_2_eq, comparator_3_eq, comparator_4_eq, comparator_5_eq,
       digital_oscilloscope_1_p2, digital_oscilloscope_1_p6, j_k_ff_1_q, n7_segment_display_1_p1,
       n7_segment_display_1_p2, n7_segment_display_2_p2;
  wire [7:0] counter_1_q;

  Clock clock_1 (.out(clock));
  Counter #(.max('h10)) counter_1 (.clr(R), .clk(clock), .Q(counter_1_q));  // open: load, up, count, D, carry
  // _7_Segment_Display 7_segment_display_1: pin names not known; wires that end beside it: n7_segment_display_1_p1, n7_segment_display_1_p2
  // BCD_to_7_Segment_decoder bcd_to_7_segment_decoder_1: pin names not known
  // _7_Segment_Display 7_segment_display_2: pin names not known; wires that end beside it: n7_segment_display_1_p2, n7_segment_display_2_p2
  // BCD_to_7_Segment_decoder bcd_to_7_segment_decoder_2: pin names not known
  // Binary_to_BCD_converter #(.binvalue(8)) binary_to_bcd_converter_1: pin names not known; wires that end beside it: counter_1_q, n7_segment_display_1_p1, n7_segment_display_1_p2
  Comparator comparator_1 (.a(8'h5), .b(counter_1_q), .eq(comparator_1_eq));  // open: gt, lt
  Comparator comparator_2 (.a(8'ha), .b(counter_1_q), .eq(comparator_2_eq));  // open: gt, lt
  _7_Segment_Display u_7_segment_display_3 ();  // open: g, f, a, b, e, d, c, dp
  // BCD_to_7_Segment_decoder bcd_to_7_segment_decoder_3: pin names not known; wires that end beside it: n7_segment_display_2_p2
  LED led_1 (.in(comparator_3_eq));
  Comparator comparator_3 (.a({8{1'b0}}), .b(counter_1_q), .eq(comparator_3_eq));  // open: gt, lt
  Comparator comparator_4 (.a(8'h2), .b(counter_1_q), .eq(comparator_4_eq));  // open: gt, lt
  Comparator comparator_5 (.a(8'ha), .b(counter_1_q), .eq(comparator_5_eq));  // open: gt, lt
  J_K_Flip_Flop j_k_ff_1 (
    .J(comparator_1_eq), .K(comparator_2_eq), .clk(clock), .Q(j_k_ff_1_q));  // open: Qn, preset, reset
  // Digital_Oscilloscope digital_oscilloscope_1: pin names not known; wires that end beside it: comparator_3_eq, digital_oscilloscope_1_p2, digital_oscilloscope_1_p2, clock, comparator_3_eq, digital_oscilloscope_1_p6
  // Buzzer buzzer_1: pin names not known; wires that end beside it: 8'ha, 14'h215, comparator_3_eq, j_k_ff_1_q
  J_K_Flip_Flop j_k_ff_2 (
    .J(comparator_4_eq), .K(comparator_5_eq), .clk(clock), .Q(digital_oscilloscope_1_p6));  // open: Qn, preset, reset
  // Buzzer buzzer_2: pin names not known; wires that end beside it: 14'h320, digital_oscilloscope_1_p6
  // Buzzer buzzer_3: pin names not known; wires that end beside it: 14'h42a, j_k_ff_1_q
endmodule

module fulladder (
  input  A,
  input  B,
  input  Carry_in,
  output sum,
  output Carry_out
);

  wire and_1_out, and_2_out, xor_1_out;

  xor xor_1 (xor_1_out, A, B);
  and and_1 (and_1_out, A, B);
  xor xor_2 (sum, xor_1_out, Carry_in);
  and and_2 (and_2_out, xor_1_out, Carry_in);
  or or_1 (Carry_out, and_2_out, and_1_out);
endmodule

module multiplex (
  input  B,
  input  A,
  input  s,
  output out_4
);

  wire and_1_out, and_2_out, not_1_out;

  not not_1 (not_1_out, s);
  and and_1 (and_1_out, not_1_out, B);
  or or_1 (out_4, and_1_out, and_2_out);
  and and_2 (and_2_out, s, A);
endmodule

module twobitadder (
  input  [1:0] A,
  input  [1:0] B,
  input  Cin,
  output [1:0] sum,
  output Cout
);

  wire fulladder_1_carry_out;

  fulladder fulladder_1 (.A(A[0]), .B(B[0]), .Carry_in(Cin), .sum(sum[0]), .Carry_out(fulladder_1_carry_out));
  fulladder fulladder_2 (.A(A[1]), .B(B[1]), .Carry_in(fulladder_1_carry_out), .sum(sum[1]), .Carry_out(Cout));
endmodule

module fourbitadder (
  input  [3:0] A,
  input  [3:0] B,
  input  Cin,
  output [3:0] sum,
  output Cout
);

  wire twobitadder_1_cout;

  twobitadder twobitadder_1 (.A(A[1:0]), .B(B[1:0]), .Cin(Cin), .sum(sum[1:0]), .Cout(twobitadder_1_cout));
  twobitadder twobitadder_2 (.A(A[3:2]), .B(B[3:2]), .Cin(twobitadder_1_cout), .sum(sum[3:2]), .Cout(Cout));
endmodule

module fulladderfortoy8 (
  input  [7:0] A,
  input  [7:0] B,
  input  Cin,
  output [7:0] sum,
  output Cout
);

  wire fourbitadder_1_cout;

  // Probe on A
  // Probe on B
  fourbitadder fourbitadder_1 (.A(A[3:0]), .B(B[3:0]), .Cin(Cin), .sum(sum[3:0]), .Cout(fourbitadder_1_cout));
  fourbitadder fourbitadder_2 (.A(A[7:4]), .B(B[7:4]), .Cin(fourbitadder_1_cout), .sum(sum[7:4]), .Cout(Cout));
  // Probe on sum
endmodule

module MUX4to1 (
  input  i0,
  input  i1,
  input  i2,
  input  i3,
  input  s0,
  input  s1,
  output out_7
);

  wire and_1_out, and_2_out, and_3_out, and_4_out, not_1_out, not_2_out;

  not not_1 (not_1_out, s0);
  not not_2 (not_2_out, s1);
  and and_1 (and_1_out, i0, not_1_out, not_2_out);
  and and_2 (and_2_out, i1, not_2_out, s0);
  and and_3 (and_3_out, i2, not_1_out, s1);
  and and_4 (and_4_out, i3, s0, s1);
  or or_1 (out_7, and_1_out, and_2_out, and_3_out, and_4_out);
endmodule

module MUX4to1_4bit (
  input  [3:0] I_0,
  input  [3:0] I_1,
  input  [3:0] I_2,
  input  [3:0] I_3,
  input  S_0,
  input  S_1,
  output [3:0] out_7
);

  MUX4to1 mux4to1_1 (.i0(I_0[0]), .i1(I_1[0]), .i2(I_2[0]), .i3(I_3[0]), .s0(S_0), .s1(S_1), .out_7(out_7[0]));
  MUX4to1 mux4to1_2 (.i0(I_0[1]), .i1(I_1[1]), .i2(I_2[1]), .i3(I_3[1]), .s0(S_0), .s1(S_1), .out_7(out_7[1]));
  MUX4to1 mux4to1_3 (.i0(I_0[2]), .i1(I_1[2]), .i2(I_2[2]), .i3(I_3[2]), .s0(S_0), .s1(S_1), .out_7(out_7[2]));
  MUX4to1 mux4to1_4 (.i0(I_0[3]), .i1(I_1[3]), .i2(I_2[3]), .i3(I_3[3]), .s0(S_0), .s1(S_1), .out_7(out_7[3]));
endmodule

module MUX_8bittoy8 (
  input  [7:0] I_0,
  input  [7:0] I_1,
  input  [7:0] I_2,
  input  [7:0] I_3,
  input  S_0,
  input  S_1,
  output [7:0] answer
);

  MUX4to1_4bit mux4to1_4bit_1 (
    .I_0(I_0[3:0]), .I_1(I_1[3:0]), .I_2(I_2[3:0]), .I_3(I_3[3:0]), .S_0(S_0), .S_1(S_1), .out_7(answer[3:0]));
  MUX4to1_4bit mux4to1_4bit_2 (
    .I_0(I_0[7:4]), .I_1(I_1[7:4]), .I_2(I_2[7:4]), .I_3(I_3[7:4]), .S_0(S_0), .S_1(S_1), .out_7(answer[7:4]));
endmodule

module DEMUX (
  input  I,
  input  S_0,
  input  S_1,
  output O_0,
  output O_1,
  output O_2,
  output O_3
);

  wire not_1_out, not_2_out;

  not not_1 (not_1_out, S_0);
  not not_2 (not_2_out, S_1);
  and and_1 (O_0, I, not_1_out, not_2_out);
  and and_2 (O_1, I, S_0, not_2_out);
  and and_3 (O_2, I, S_1, not_1_out);
  and and_4 (O_3, I, S_0, S_1);
endmodule

module DMUX_toy8 (
  input  [7:0] I,
  input  S_0,
  input  S_1,
  output [7:0] O_0,
  output [7:0] O_1,
  output [7:0] O_2,
  output [7:0] O_3
);

  DEMUX demux_1 (.I(I[0]), .S_0(S_0), .S_1(S_1), .O_0(O_0[0]), .O_1(O_1[0]), .O_2(O_2[0]), .O_3(O_3[0]));
  DEMUX demux_2 (.I(I[1]), .S_0(S_0), .S_1(S_1), .O_0(O_0[1]), .O_1(O_1[1]), .O_2(O_2[1]), .O_3(O_3[1]));
  DEMUX demux_3 (.I(I[2]), .S_0(S_0), .S_1(S_1), .O_0(O_0[2]), .O_1(O_1[2]), .O_2(O_2[2]), .O_3(O_3[2]));
  DEMUX demux_4 (.I(I[3]), .S_0(S_0), .S_1(S_1), .O_0(O_0[3]), .O_1(O_1[3]), .O_2(O_2[3]), .O_3(O_3[3]));
  DEMUX demux_5 (.I(I[4]), .S_0(S_0), .S_1(S_1), .O_0(O_0[4]), .O_1(O_1[4]), .O_2(O_2[4]), .O_3(O_3[4]));
  DEMUX demux_6 (.I(I[5]), .S_0(S_0), .S_1(S_1), .O_0(O_0[5]), .O_1(O_1[5]), .O_2(O_2[5]), .O_3(O_3[5]));
  DEMUX demux_7 (.I(I[6]), .S_0(S_0), .S_1(S_1), .O_0(O_0[6]), .O_1(O_1[6]), .O_2(O_2[6]), .O_3(O_3[6]));
  DEMUX demux_8 (.I(I[7]), .S_0(S_0), .S_1(S_1), .O_0(O_0[7]), .O_1(O_1[7]), .O_2(O_2[7]), .O_3(O_3[7]));
endmodule

module ALU_toy8 (
  input  [7:0] A,
  input  [7:0] B,
  input  S2,
  input  S1,
  input  S0,
  output [7:0] result
);

  wire de_coder_1_i, de_coder_1_ii, de_coder_1_iii, de_coder_1_iv, de_coder_1_v, de_coder_1_vi, undriven;
  wire [7:0] andgate_8bit_1_result, full_sub8bit_1_result, fulladderfortoy8_1_sum, leftshift_1_out_2,
       rightshift_1_out_2, xorgate_8bit_1_result;

  // Probe on B
  // Probe on A
  fulladderfortoy8 fulladderfortoy8_1 (.A(A), .B(B), .sum(fulladderfortoy8_1_sum));  // open: Cin, Cout
  xorgate_8bit xorgate_8bit_1 (.A(A), .B(B), .result(xorgate_8bit_1_result));
  andgate_8bit andgate_8bit_1 (.A(A), .B(B), .result(andgate_8bit_1_result));
  RightShift rightshift_1 (.in_1(A), .out_2(rightshift_1_out_2));
  LeftShift leftshift_1 (.in_1(A), .out_2(leftshift_1_out_2));
  FULL_SUB8BIT full_sub8bit_1 (.A(A), .B(B), .result(full_sub8bit_1_result));  // open: B_in, B_out
  De_coder de_coder_1 (
    .I2(S2), .I1(S1), .I0(S0), .in_4(undriven), .i(de_coder_1_i), .ii(de_coder_1_ii), .iii(de_coder_1_iii),
    .iv(de_coder_1_iv), .v(de_coder_1_v), .vi(de_coder_1_vi));  // open: O, vii
  one_hot_mux one_hot_mux_1 (
    .A(fulladderfortoy8_1_sum), .B(xorgate_8bit_1_result), .C(andgate_8bit_1_result), .D(rightshift_1_out_2),
    .E(leftshift_1_out_2), .F(full_sub8bit_1_result), .I1(de_coder_1_i), .I2(de_coder_1_ii),
    .I3(de_coder_1_iii), .I4(de_coder_1_iv), .I5(de_coder_1_v), .I6(de_coder_1_vi), .decision(result));
  // Probe on result
endmodule

module one_hot_mux (
  input  [7:0] A,
  input  [7:0] B,
  input  [7:0] C,
  input  [7:0] D,
  input  [7:0] E,
  input  [7:0] F,
  input  I1,
  input  I2,
  input  I3,
  input  I4,
  input  I5,
  input  I6,
  output [7:0] decision
);

  wire [7:0] andgate_8bit_1_result, andgate_8bit_2_result, andgate_8bit_3_result, andgate_8bit_4_result,
       andgate_8bit_5_result, andgate_8bit_6_result, or_1_out, or_2_out;

  andgate_8bit andgate_8bit_1 (.A(A), .B({8{I1}}), .result(andgate_8bit_1_result));
  andgate_8bit andgate_8bit_2 (.A(B), .B({8{I2}}), .result(andgate_8bit_2_result));
  andgate_8bit andgate_8bit_3 (.A(C), .B({8{I3}}), .result(andgate_8bit_3_result));
  andgate_8bit andgate_8bit_4 (.A(D), .B({8{I4}}), .result(andgate_8bit_4_result));
  andgate_8bit andgate_8bit_5 (.A(E), .B({8{I5}}), .result(andgate_8bit_5_result));
  andgate_8bit andgate_8bit_6 (.A(F), .B({8{I6}}), .result(andgate_8bit_6_result));
  assign or_1_out = andgate_8bit_1_result | andgate_8bit_2_result | andgate_8bit_3_result;  // OR_Gate or_1, 8 bits wide
  assign or_2_out = andgate_8bit_4_result | andgate_8bit_5_result | andgate_8bit_6_result;  // OR_Gate or_2, 8 bits wide
  orgate_8bit orgate_8bit_1 (.A(or_1_out), .B(or_2_out), .result(decision));
endmodule

module andgate_8bit (
  input  [7:0] A,
  input  [7:0] B,
  output [7:0] result
);

  andgate andgate_1 (.A(A[0]), .B(B[0]), .out_3(result[0]));
  andgate andgate_2 (.A(A[1]), .B(B[1]), .out_3(result[1]));
  andgate andgate_3 (.A(A[2]), .B(B[2]), .out_3(result[2]));
  andgate andgate_4 (.A(A[3]), .B(B[3]), .out_3(result[3]));
  andgate andgate_5 (.A(A[4]), .B(B[4]), .out_3(result[4]));
  andgate andgate_6 (.A(A[5]), .B(B[5]), .out_3(result[5]));
  andgate andgate_7 (.A(A[6]), .B(B[6]), .out_3(result[6]));
  andgate andgate_8 (.A(A[7]), .B(B[7]), .out_3(result[7]));
endmodule

module orgate_8bit (
  input  [7:0] A,
  input  [7:0] B,
  output [7:0] result
);

  orgate orgate_1 (.A(A[0]), .B(B[0]), .orout(result[0]));
  orgate orgate_2 (.A(A[1]), .B(B[1]), .orout(result[1]));
  orgate orgate_3 (.A(A[2]), .B(B[2]), .orout(result[2]));
  orgate orgate_4 (.A(A[3]), .B(B[3]), .orout(result[3]));
  orgate orgate_5 (.A(A[4]), .B(B[4]), .orout(result[4]));
  orgate orgate_6 (.A(A[5]), .B(B[5]), .orout(result[5]));
  orgate orgate_7 (.A(A[6]), .B(B[6]), .orout(result[6]));
  orgate orgate_8 (.A(A[7]), .B(B[7]), .orout(result[7]));
endmodule

module xorgate_8bit (
  input  [7:0] A,
  input  [7:0] B,
  output [7:0] result
);

  xorimplement xorimplement_1 (.A(A[0]), .B(B[0]), .xorout(result[0]));
  xorimplement xorimplement_2 (.A(A[1]), .B(B[1]), .xorout(result[1]));
  xorimplement xorimplement_3 (.A(A[2]), .B(B[2]), .xorout(result[2]));
  xorimplement xorimplement_4 (.A(A[3]), .B(B[3]), .xorout(result[3]));
  xorimplement xorimplement_5 (.A(A[4]), .B(B[4]), .xorout(result[4]));
  xorimplement xorimplement_6 (.A(A[5]), .B(B[5]), .xorout(result[5]));
  xorimplement xorimplement_7 (.A(A[6]), .B(B[6]), .xorout(result[6]));
  xorimplement xorimplement_8 (.A(A[7]), .B(B[7]), .xorout(result[7]));
endmodule

module notgate_8bit (
  input  [7:0] A,
  output [7:0] result
);

  notgate notgate_1 (.in_1(A[0]), .out_2(result[0]));
  notgate notgate_2 (.in_1(A[1]), .out_2(result[1]));
  notgate notgate_3 (.in_1(A[2]), .out_2(result[2]));
  notgate notgate_4 (.in_1(A[3]), .out_2(result[3]));
  notgate notgate_5 (.in_1(A[4]), .out_2(result[4]));
  notgate notgate_6 (.in_1(A[5]), .out_2(result[5]));
  notgate notgate_7 (.in_1(A[6]), .out_2(result[6]));
  notgate notgate_8 (.in_1(A[7]), .out_2(result[7]));
endmodule

module De_coder (
  input  I2,
  input  I1,
  input  I0,
  input  in_4,
  output O,
  output i,
  output ii,
  output iii,
  output iv,
  output v,
  output vi,
  output vii
);

  wire not_1_out, not_2_out, not_3_out, not_4_out, not_5_out, not_6_out, not_7_out;

  // Probe on {I2, I1, I0}
  not not_1 (not_1_out, I2);
  not not_2 (not_2_out, I2);
  not not_3 (not_3_out, I1);
  not not_4 (not_4_out, I0);
  not not_5 (not_5_out, I2);
  not not_6 (not_6_out, I0);
  not not_7 (not_7_out, I1);
  and and_1 (i, I0, not_3_out, not_1_out);
  and and_2 (ii, not_4_out, I1, not_5_out);
  and and_3 (iii, I0, I1, not_2_out);
  and and_4 (iv, not_6_out, not_7_out, I2);
  and and_5 (v, I0, ~I1, I2);  // AND_Gate
  and and_6 (vi, ~I0, I1, I2);  // AND_Gate
  and and_7 (vii, I0, I1, I2);
  nor nor_1 (O, I0, I2, I1);
endmodule

module Half_adder (
  input  A,
  input  B,
  output S
);

  xorimplement xorimplement_1 (.A(A), .B(B), .xorout(S));
endmodule

module MAJ (
  input  in_1,
  input  in_2,
  input  Cin,
  output cout
);

  wire andgate_1_out_3, andgate_2_out_3, orgate_1_orout;

  andgate andgate_1 (.A(in_1), .B(in_2), .out_3(andgate_1_out_3));
  orgate orgate_1 (.A(in_1), .B(in_2), .orout(orgate_1_orout));
  andgate andgate_2 (.A(Cin), .B(orgate_1_orout), .out_3(andgate_2_out_3));
  orgate orgate_2 (.A(andgate_2_out_3), .B(andgate_1_out_3), .orout(cout));
endmodule

module ODD (
  input  in_1,
  input  in_2,
  input  Cin,
  output out_4
);

  wire andgate_1_out_3, andgate_2_out_3, notgate_1_out_2, notgate_2_out_2, xorimplement_1_xorout;

  xorimplement xorimplement_1 (.A(in_1), .B(in_2), .xorout(xorimplement_1_xorout));
  notgate notgate_1 (.in_1(Cin), .out_2(notgate_1_out_2));
  notgate notgate_2 (.in_1(xorimplement_1_xorout), .out_2(notgate_2_out_2));
  andgate andgate_1 (.A(xorimplement_1_xorout), .B(notgate_1_out_2), .out_3(andgate_1_out_3));
  andgate andgate_2 (.A(notgate_2_out_2), .B(Cin), .out_3(andgate_2_out_3));
  orgate orgate_1 (.A(andgate_1_out_3), .B(andgate_2_out_3), .orout(out_4));
endmodule

module Full_SUB (
  input  A,
  input  B,
  input  B_in,
  output Diff,
  output B_out
);

  wire and_1_out, and_2_out, not_1_out, not_2_out, xor_1_out;

  xor xor_1 (xor_1_out, A, B);
  not not_1 (not_1_out, A);
  and and_1 (and_1_out, not_1_out, B);
  xor xor_2 (Diff, xor_1_out, B_in);
  not not_2 (not_2_out, xor_1_out);
  and and_2 (and_2_out, not_2_out, B_in);
  or or_1 (B_out, and_2_out, and_1_out);
endmodule

module FULL_SUB8BIT (
  input  [7:0] A,
  input  [7:0] B,
  input  B_in,
  output [7:0] result,
  output B_out
);

  wire full_sub_1_b_out, full_sub_2_b_out, full_sub_3_b_out, full_sub_4_b_out, full_sub_5_b_out,
       full_sub_6_b_out, full_sub_7_b_out;

  // Probe on A
  // Probe on B
  // Probe on result
  Full_SUB full_sub_1 (.A(A[0]), .B(B[0]), .B_in(B_in), .Diff(result[0]), .B_out(full_sub_1_b_out));
  Full_SUB full_sub_2 (.A(A[1]), .B(B[1]), .B_in(full_sub_1_b_out), .Diff(result[1]), .B_out(full_sub_2_b_out));
  Full_SUB full_sub_3 (.A(A[2]), .B(B[2]), .B_in(full_sub_2_b_out), .Diff(result[2]), .B_out(full_sub_3_b_out));
  Full_SUB full_sub_4 (.A(A[3]), .B(B[3]), .B_in(full_sub_3_b_out), .Diff(result[3]), .B_out(full_sub_4_b_out));
  Full_SUB full_sub_5 (.A(A[4]), .B(B[4]), .B_in(full_sub_4_b_out), .Diff(result[4]), .B_out(full_sub_5_b_out));
  Full_SUB full_sub_6 (.A(A[5]), .B(B[5]), .B_in(full_sub_5_b_out), .Diff(result[5]), .B_out(full_sub_6_b_out));
  Full_SUB full_sub_7 (.A(A[6]), .B(B[6]), .B_in(full_sub_6_b_out), .Diff(result[6]), .B_out(full_sub_7_b_out));
  Full_SUB full_sub_8 (.A(A[7]), .B(B[7]), .B_in(full_sub_7_b_out), .Diff(result[7]), .B_out(B_out));
endmodule

module RightShift (
  input  [7:0] in_1,
  output [7:0] out_2
);

  Pull_Resistor pull_resistor_1 (.node(out_2[7]));

  assign out_2[6:0] = in_1[7:1];
endmodule

module LeftShift (
  input  [7:0] in_1,
  output [7:0] out_2
);

  Pull_Resistor pull_resistor_1 (.node(out_2[0]));

  assign out_2[7:1] = in_1[6:0];
endmodule

module NAND_WITH_TWOTRANSISTOR (
  input  A,
  input  B,
  output out_3
);

  wire transistor_2_out;

  Pull_Resistor #(.pull(1)) pull_resistor_1 (.node(out_3));
  Transistor #(.\type ("n")) transistor_1 (.in(transistor_2_out), .out(out_3), .gate(A));
  Transistor #(.\type ("n")) transistor_2 (.in(1'b0), .out(transistor_2_out), .gate(B));
endmodule

module NOR_WITH_TWOTRANSISTOR (
  input  A,
  input  B,
  output out_3
);

  wire transistor_2_out;

  Pull_Resistor pull_resistor_1 (.node(out_3));
  Transistor transistor_1 (.in(transistor_2_out), .out(out_3), .gate(A));
  Transistor transistor_2 (.in(1'b1), .out(transistor_2_out), .gate(B));
endmodule

module Ripple_carry_adder (
  input  A,
  input  B,
  input  Cin,
  output Sum,
  output Cout
);

  ODD odd_1 (.in_1(A), .in_2(B), .Cin(Cin), .out_4(Sum));
  MAJ maj_1 (.in_1(A), .in_2(B), .Cin(Cin), .cout(Cout));
endmodule

module AND3INPUT (
  input  A,
  input  B,
  input  C,
  output res
);

  wire nand_with_twotransistor_1_out_3, nand_with_twotransistor_2_out_3, notgate_1_out_2;

  NAND_WITH_TWOTRANSISTOR nand_with_twotransistor_1 (.A(A), .B(B), .out_3(nand_with_twotransistor_1_out_3));
  notgate notgate_1 (.in_1(nand_with_twotransistor_1_out_3), .out_2(notgate_1_out_2));
  NAND_WITH_TWOTRANSISTOR nand_with_twotransistor_2 (
    .A(notgate_1_out_2), .B(C), .out_3(nand_with_twotransistor_2_out_3));
  notgate notgate_2 (.in_1(nand_with_twotransistor_2_out_3), .out_2(res));
endmodule

module OR3INPUT (
  input  A,
  input  B,
  input  C,
  output res
);

  wire nor_with_twotransistor_1_out_3, nor_with_twotransistor_2_out_3, notgate_1_out_2;

  NOR_WITH_TWOTRANSISTOR nor_with_twotransistor_1 (.A(A), .B(B), .out_3(nor_with_twotransistor_1_out_3));
  notgate notgate_1 (.in_1(nor_with_twotransistor_1_out_3), .out_2(notgate_1_out_2));
  NOR_WITH_TWOTRANSISTOR nor_with_twotransistor_2 (.A(notgate_1_out_2), .B(C), .out_3(nor_with_twotransistor_2_out_3));
  notgate notgate_2 (.in_1(nor_with_twotransistor_2_out_3), .out_2(res));
endmodule

module XNOR_8bit (
  input  [7:0] A,
  input  [7:0] B,
  output [7:0] res
);

  wire [7:0] xorgate_8bit_1_result;

  xorgate_8bit xorgate_8bit_1 (.A(A), .B(B), .result(xorgate_8bit_1_result));
  notgate_8bit notgate_8bit_1 (.A(xorgate_8bit_1_result), .result(res));
endmodule
